# Fritzing sketch irrigador-v1 (saved by Fritzing 0.9.6b)

parts:
  WATER_PUMP1 = water pump/motor
  Tiny_RTC1 = Tiny RTC
  Part2 = Arduino Uno (Rev3) - ICSP
  Mod1 = KY-019 5V Relay Module [package="Breakout board"]

nets:
  N1: WATER_PUMP1.pin_2, Mod1.NO
  N2: Tiny_RTC1.SCL, Part2.A5/SCL
  N3: Tiny_RTC1.SDA, Part2.A4/SDA
  N4: Tiny_RTC1.VCC#3, Part2.5V
  N5: Tiny_RTC1.GND#4, Part2.GND
  N6: Tiny_RTC1.VCC#9, Mod1.+
  N7: Tiny_RTC1.GND#10, Mod1.-
  N8: Part2.D7, Mod1.S

custom parts:
  water pump/motor: WATER PUMP BY ARDUBLOCKTR
  Tiny RTC: Tiny RTC I2C module DS1370Z RTC and AT24C32 EEPROM
  KY-019 5V Relay Module: KY-019 5V Relay module, used to control AC circuits. (Special thanks to vanepp for fixing the PCB holes and other errors)
